# Fritzing sketch farming (saved by Fritzing 0.9.3b)
breadboards: 1

parts:
  U1 = NodeMCU V3.0
  Part2 = KY-015 Temperature & Humidity Sensor Module [package="Breakout board"]
  Part3 = FC-28 Soil Hygrometer Module
  Part4 = FC-28 Soil Hygrometer Module - Probe

nets:
  N1: U1.D0, Part2.S
  3V3: U1.3V3, Part2.Vin, Part3.VCC
  GND: U1.GND, Part2.-, Part3.GND
  N2: U1.A0, Part3.AO
  N3: Part3.POS, Part4.POS
  N4: Part3.NEG, Part4.NEG

custom parts:
  NodeMCU V3.0: NodeMcu V3 Lua WIFI Development Board
  KY-015 Temperature & Humidity Sensor Module: KY-015 temperature and humidity sensor module, provides a low-latency serial interface to measure humidity and temperature.
  FC-28 Soil Hygrometer Module: The FC-28 is a soil hygrometer module that uses the Texas Instruments LM393 comparator chip to provide an analog measurement of soil humidity. The digital output is high when soil moisture is over a certain threshold, as determined by adjusting the potentiometer.
  FC-28 Soil Hygrometer Module - Probe: The FC-28 is a soil hygrometer module that uses the Texas Instruments LM393 comparator chip to provide an analog measurement of soil humidity.
